# Fritzing sketch Sump Pump Monitor-No Network (saved by Fritzing 0.9.3b)
breadboards: 1

parts:
  Part1 = Arduino Uno (Rev3)
  LED1 = LED - 5mm [color="Blue (430nm)" package="5 mm [THT]"]
  LED2 = LED - 5mm [color="Red (633nm)" package="5 mm [THT]"]
  LED3 = LED - 5mm [color="Green (555nm)" package="5 mm [THT]"]
  LED4 = LED - 5mm [color="Yellow (595nm)" package="5 mm [THT]"]
  R1 = Resistor [tolerance=±5% resistance=330 package=THT]
  R2 = Resistor [tolerance=±5% resistance=330 package=THT]
  R3 = Resistor [tolerance=±5% resistance=330 package=THT]
  R4 = Resistor [tolerance=±5% resistance=330 package=THT]
  S4 = Tilt Switch [package=THT]
  S5 = Tilt Switch [package=THT]
  S6 = Tilt Switch [package=THT]
  R5 = Resistor [tolerance=±5% resistance=10k package=THT]
  R6 = Resistor [tolerance=±5% resistance=10k package=THT]
  R7 = Resistor [tolerance=±5% resistance=10k package=THT]
  S7 = Pushbutton [package="[THT]"]
  R8 = Resistor [tolerance=±5% resistance=10k package=THT]
  J1 = Piezo Speaker

nets:
  N1: Part1.A0, S4.Pin_1, R5.Pin_0
  N2: Part1.A1, S5.Pin_1, R6.Pin_0
  N3: Part1.A2, S6.Pin_1, R7.Pin_0
  N4: Part1.A5/SCL, S7.Pin_3, S7.Pin_4, R8.Pin_0
  N5: Part1.D2, R3.Pin_0
  N6: Part1.D3_PWM, R2.Pin_0
  N7: Part1.D5_PWM, R1.Pin_0
  N8: Part1.D6_PWM, R4.Pin_0
  N9: Part1.D7, J1.pin2
  N10: Part1.5V, S4.Pin_2, S5.Pin_2, S6.Pin_2, S7.Pin_1, S7.Pin_2
  N11: Part1.GND, LED1.cathode, LED2.cathode, LED3.cathode, LED4.cathode, R5.Pin_1, R6.Pin_1, R7.Pin_1, R8.Pin_1, J1.pin1
  N12: LED1.anode, R1.Pin_1
  N13: LED2.anode, R2.Pin_1
  N14: LED3.anode, R4.Pin_1
  N15: LED4.anode, R3.Pin_1
